# Fritzing sketch drone_electronics (saved by Fritzing 1.0.4)

parts:
  MPU6050_ACCEL-GYRO = InvenSense MPU6050
  U1 = LIPO-110mAh [package=lipo-110]
  FR = DC Motor [voltage_(max)=6V voltage_(min)=3V]
  FL = DC Motor [voltage_(max)=6V voltage_(min)=3V]
  BR = DC Motor [voltage_(max)=6V voltage_(min)=3V]
  BL = DC Motor [voltage_(max)=6V voltage_(min)=3V]
  D1 = Schottky Diode [part_number=1N5817 package="300 mil [THT]"]
  D2 = Schottky Diode [part_number=1N5817 package="300 mil [THT]"]
  D3 = Schottky Diode [part_number=1N5817 package="300 mil [THT]"]
  D4 = Schottky Diode [part_number=1N5817 package="300 mil [THT]"]
  Q1 = MOSFET-NCHANNEL [package=to220v]
  Q2 = Basic FET N-Channel [package="DPak [SMD]"]
  Q3 = Basic FET N-Channel [package="DPak [SMD]"]
  Q4 = Basic FET N-Channel [package="DPak [SMD]"]
  R1 = Resistor [tolerance=±5% resistance=220 package="1206 [SMD]"]  # not connected
  R3 = 10 KΩ Resistor [package="1206 [SMD]"]
  R4 = 10 KΩ Resistor [package="1206 [SMD]"]
  R5 = 10 KΩ Resistor [package="1206 [SMD]"]
  R6 = 10 KΩ Resistor [package="1206 [SMD]"]
  Arduino_PRO_mini_3_3V_8MHz = Arduino Pro Mini (3.3V)
  NRF24L01_RF_comms = NRF24L01+ Breakout Board
  100uF = Capacitor Polarized [package=cpol-radial-1000uf-63v]
  100_nF = Capacitor [package=cap-pth-small2]

nets:
  VCC: MPU6050_ACCEL-GYRO.VCC, U1.+, FR.pin_1, FL.pin_2, BR.pin_2, BL.pin_1, D1.cathode, D2.cathode, D3.cathode, D4.cathode, Arduino_PRO_mini_3_3V_8MHz.VCC, NRF24L01_RF_comms.VCC, 100uF.+, 100_nF.2
  GND: MPU6050_ACCEL-GYRO.GND, U1.-, Q1.S, Q2.source, Q3.source, Q4.source, R3.Pin_1, R4.Pin_0, R5.Pin_1, R6.Pin_1, Arduino_PRO_mini_3_3V_8MHz.GND, NRF24L01_RF_comms.GND, 100uF.-, 100_nF.1
  N1: MPU6050_ACCEL-GYRO.SCL, Arduino_PRO_mini_3_3V_8MHz.A5
  N2: MPU6050_ACCEL-GYRO.SDA, Arduino_PRO_mini_3_3V_8MHz.A4
  N3: FR.pin_2, D4.anode, Q4.drain
  N4: FL.pin_1, D3.anode, Q3.drain
  N5: BR.pin_1, D2.anode, Q2.drain
  N6: BL.pin_2, D1.anode, Q1.D
  N7: Q1.G, R3.Pin_0, Arduino_PRO_mini_3_3V_8MHz.D5
  N8: Q2.Gate, R4.Pin_1, Arduino_PRO_mini_3_3V_8MHz.D3
  N9: Q3.Gate, R5.Pin_0, Arduino_PRO_mini_3_3V_8MHz.D6
  N10: Q4.Gate, R6.Pin_0, Arduino_PRO_mini_3_3V_8MHz.D9
  N11: Arduino_PRO_mini_3_3V_8MHz.SCK, NRF24L01_RF_comms.SCK
  N12: Arduino_PRO_mini_3_3V_8MHz.MISO, NRF24L01_RF_comms.MISO
  N13: Arduino_PRO_mini_3_3V_8MHz.MOSI, NRF24L01_RF_comms.MOSI
  N14: Arduino_PRO_mini_3_3V_8MHz.D10, NRF24L01_RF_comms.CS
  N15: Arduino_PRO_mini_3_3V_8MHz.D7, NRF24L01_RF_comms.CE

notes:
  -720 coreless motors
  -schottky diodes SB-240
  -N-mosfet, AO3400
  -10KΩ SMD resistors
  Li-Po battery 3.7 V, 500mAh
  BOTH BREADBOARD AND PCB NOT FOR USE,
  was only interested in schematic since structure was 3D and done by hand

custom parts:
  10 KΩ Resistor: A generic resistor
